# Fritzing sketch raspberrypi-sensors (saved by Fritzing 0.9.4)
breadboards: 1

parts:
  Raspberry_Pi1 = Raspberry Pi 2
  BME280 = BMP280
  ADC1 = MCP3008 [package=dil16]
  R1 = Resistor [tolerance=±5% resistance=10k package=THT]
  R2 = PHOTOCELL [package=photocell]

nets:
  3V3: Raspberry_Pi1.3v3, BME280.VIN, ADC1.VREF, ADC1.VDD, R2.P$1
  N1: Raspberry_Pi1.GPIO2, BME280.SDA
  N2: Raspberry_Pi1.GPIO3, BME280.SCL
  N3: Raspberry_Pi1.GPIO10, ADC1.Din
  N4: Raspberry_Pi1.GPIO9, ADC1.Dout
  N5: Raspberry_Pi1.GPIO11, ADC1.CLK
  N6: Raspberry_Pi1.GPIO8, ADC1.CS/SHDN
  GND: Raspberry_Pi1.GND, BME280.GND, ADC1.DGND, ADC1.AGND, R1.Pin_1
  N7: ADC1.CH0, R1.Pin_0, R2.P$2

custom parts:
  BMP280: Temperature Humidity Barometric presure Sensor, I2C
